// Logisim project CPU.circ as structural Verilog: 14 circuits, main circuit cpu
module cpu (
  input  [7:0] entrada,
  output [7:0] saida,
  output PROC_clk,
  output PROC_fetch
);

  wire AC_INPUT_RAM, AC_OUTPUT_RAM, and_1_out, and_2_out, and_3_out, and_4_out, and_5_out, and_6_out,
       and_7_out, and_8_out, and_9_out, c3, c4, COMP, d_ff_1_qn, EE_RAM, M1_CTR8, M3, nand_1_out, not_1_out,
       not_2_out, not_3_out, not_4_out, not_5_out, not_6_out, not_7_out, not_8_out, OP, or_1_out, or_2_out,
       PARAR, PRINT, R_AC;
  wire [7:0] AC, demultiplexer_1_out0, demultiplexer_1_out1, EE, EE_Conteudo, multiplexer_1_out,
       multiplexer_2_out, multiplexer_3_out, multiplexer_4_out, PC_q, ula_1_r;
  wire [15:0] IR, ram_1_dout;

  D_Flip_Flop d_ff_1 (.D(d_ff_1_qn), .clk(PROC_clk), .Q(PROC_fetch), .Qn(d_ff_1_qn));  // open: preset, reset
  Clock clock_1 (.out(PROC_clk));
  and and_1 (and_1_out, PROC_clk, PARAR);
  and and_2 (and_2_out, PROC_fetch, not_1_out);
  not not_1 (not_1_out, PROC_clk);
  Counter PC (.clr(and_1_out), .load(M1_CTR8), .up(1'b1), .clk(and_2_out), .D(EE), .Q(PC_q));  // open: count, carry
  UC uc_1 (
    .IR(IR), .c3(c3), .c4(c4), .M3(M3), .EE(EE), .R_AC(R_AC), .OP(OP), .AC_OUTPUT_RAM(AC_OUTPUT_RAM),
    .AC_INPUT_RAM(AC_INPUT_RAM), .PRINT(PRINT), .PARAR(PARAR), .COMP(COMP), .M1_CTR8(M1_CTR8), .EE_RAM(EE_RAM));
  nand nand_1 (nand_1_out, PROC_clk, PROC_fetch);
  and and_3 (and_3_out, nand_1_out, EE_RAM);
  not not_2 (not_2_out, PROC_fetch);
  Multiplexer #(.width(8)) multiplexer_1 (.in0(PC_q), .in1(EE), .out(multiplexer_1_out), .sel(or_1_out));
  or or_1 (or_1_out, and_3_out, M1_CTR8);
  not not_3 (not_3_out, PROC_clk);
  Multiplexer #(.width(8)) multiplexer_2 (.in0(entrada), .in1(AC), .out(multiplexer_2_out), .sel(AC_INPUT_RAM));
  and and_4 (and_4_out, M3, not_2_out);
  RAM #(.asyncread("true"), .dataWidth(16)) ram_1 (
    .addr(multiplexer_1_out), .we(and_4_out), .clk(not_3_out), .din({{8{1'b0}}, multiplexer_2_out}),
    .dout(ram_1_dout));  // open: oe
  Multiplexer #(.width(8)) multiplexer_3 (.in0(EE_Conteudo), .in1({8{1'b0}}), .out(multiplexer_3_out), .sel(COMP));
  Demultiplexer #(.width(8)) demultiplexer_1 (
    .out0(demultiplexer_1_out0), .out1(demultiplexer_1_out1), .in(ram_1_dout[7:0]), .sel(AC_OUTPUT_RAM));
  ULA ula_1 (.A(AC), .B(multiplexer_3_out), .OP(OP), .R(ula_1_r), .c3(c3), .c4(c4));  // open: o1, o2, c0, c1, c2, c5
  not not_4 (not_4_out, PROC_clk);
  and and_5 (and_5_out, not_4_out, PROC_fetch);
  not not_5 (not_5_out, PROC_clk);
  not not_6 (not_6_out, PROC_fetch);
  Multiplexer #(.width(8)) multiplexer_4 (
    .in0(demultiplexer_1_out1), .in1(ula_1_r), .out(multiplexer_4_out), .sel(R_AC));
  Register #(.width(16)) u_IR (.D(ram_1_dout), .clk(and_5_out), .Q(IR), .clr(and_7_out));  // open: en
  Demultiplexer #(.width(8)) demultiplexer_2 (
    .out0(EE_Conteudo), .out1(saida), .in(demultiplexer_1_out0), .sel(and_6_out));
  and and_6 (and_6_out, not_5_out, not_6_out, PRINT);
  and and_7 (and_7_out, PROC_clk, PARAR);
  or or_2 (or_2_out, AC_OUTPUT_RAM, R_AC);
  not not_7 (not_7_out, PROC_clk);
  and and_8 (and_8_out, not_7_out, or_2_out, not_8_out);
  not not_8 (not_8_out, PROC_fetch);
  Register u_AC (.D(multiplexer_4_out), .clk(and_8_out), .Q(AC), .clr(and_9_out));  // open: en
  and and_9 (and_9_out, PROC_clk, PARAR);

  // Other names for the same wires on the sheet: clk = PROC_clk; ftc = PROC_fetch

  // Notes on the sheet:
  //   Memória RAM
endmodule

module UC (
  input  [15:0] IR,
  input  c3,
  input  c4,
  output M3,
  output [7:0] EE,
  output R_AC,
  output OP,
  output AC_OUTPUT_RAM,
  output AC_INPUT_RAM,
  output PRINT,
  output PARAR,
  output COMP,
  output M1_CTR8,
  output EE_RAM
);

  wire decoder_1_out1, decoder_1_out2, decoder_1_out3, decoder_1_out4, decoder_1_out7, decoder_1_out8,
       decoder_1_out10, decoder_1_out11, decoder_1_out13, decoder_1_out15, instrucao_1_1_ee_ram_1,
       instrucao_2_1_ee_ram_2, instrucao_2_1_m3_2, instrucao_3_e_4_1_ee_ram, instrucao_7_1_ee_ram_7,
       instrucao_7_1_m3_7, instrucao_8_1_ee_ram_8, nor_1_out;

  nor nor_1 (nor_1_out, IR[12], IR[13], IR[14], IR[15]);
  Decoder #(.select(4)) decoder_1 (
    .out1(decoder_1_out1), .out2(decoder_1_out2), .out3(decoder_1_out3), .out4(decoder_1_out4),
    .out7(decoder_1_out7), .out8(decoder_1_out8), .out9(PARAR), .out10(decoder_1_out10),
    .out11(decoder_1_out11), .out13(decoder_1_out13), .out15(decoder_1_out15), .sel(IR[11:8]), .en(nor_1_out));  // open: out0, out5, out6, out12, out14
  Instrucao_1 instrucao_1_1 (.I1(decoder_1_out1), .EE_RAM_1(instrucao_1_1_ee_ram_1), .AC_OUTPUT_RAM_1(AC_OUTPUT_RAM));
  Instrucao_2 instrucao_2_1 (
    .I2(decoder_1_out2), .M3_2(instrucao_2_1_m3_2), .EE_RAM_2(instrucao_2_1_ee_ram_2),
    .AC_INPUT_RAM_2(AC_INPUT_RAM));
  Instrucao_3_e_4 instrucao_3_e_4_1 (
    .I3(decoder_1_out3), .I4(decoder_1_out4), .R_AC(R_AC), .OP(OP), .EE_RAM(instrucao_3_e_4_1_ee_ram));
  Instrucao_7 instrucao_7_1 (.I7(decoder_1_out7), .EE_RAM_7(instrucao_7_1_ee_ram_7), .M3_7(instrucao_7_1_m3_7));
  Instrucao_8 instrucao_8_1 (.I8(decoder_1_out8), .EE_RAM_8(instrucao_8_1_ee_ram_8), .PRINT(PRINT));
  Instrucao_A_ate_F instrucao_a_ate_f_1 (
    .IA(decoder_1_out10), .IB(decoder_1_out11), .ID(decoder_1_out13), .I_F(decoder_1_out15), .c3(c3),
    .c4(c4), .COMP(COMP), .M1_CTR8(M1_CTR8));
  or or_1 (EE_RAM, instrucao_8_1_ee_ram_8, instrucao_7_1_ee_ram_7, instrucao_3_e_4_1_ee_ram, instrucao_2_1_ee_ram_2, instrucao_1_1_ee_ram_1);
  or or_2 (M3, instrucao_2_1_m3_2, instrucao_7_1_m3_7);

  assign EE = IR[7:0];

  // Other names for the same wires on the sheet: INSTR[3:0] = IR[11:8]
endmodule

module ULA (
  input  [7:0] A,
  input  [7:0] B,
  input  OP,
  output [7:0] R,
  output o1,
  output o2,
  output c0,
  output c1,
  output c2,
  output c3,
  output c4,
  output c5
);

  OP_Aritmetico_8bit op_aritmetico_8bit_1 (.A(A), .B(B), .OP(OP), .R(R), .CS(o2), .SS(o1));
  Comp_8bit comp_8bit_1 (.A(A), .B(B), .c0(c0), .c1(c1), .c2(c2), .c3(c3), .c4(c4), .c5(c5));
endmodule

module Instrucao_1 (
  input  I1,
  output EE_RAM_1,
  output AC_OUTPUT_RAM_1
);


  assign AC_OUTPUT_RAM_1 = I1;
  assign EE_RAM_1 = I1;
endmodule

module Instrucao_2 (
  input  I2,
  output M3_2,
  output EE_RAM_2,
  output AC_INPUT_RAM_2
);


  assign AC_INPUT_RAM_2 = I2;
  assign EE_RAM_2 = I2;
  assign M3_2 = I2;
endmodule

module Instrucao_3_e_4 (
  input  I3,
  input  I4,
  output R_AC,
  output OP,
  output EE_RAM
);

  or or_1 (EE_RAM, I3, I4);

  assign OP = I4;
  assign R_AC = EE_RAM;
endmodule

module Instrucao_7 (
  input  I7,
  output EE_RAM_7,
  output M3_7
);


  assign EE_RAM_7 = I7;
  assign M3_7 = I7;
endmodule

module Instrucao_8 (
  input  I8,
  output EE_RAM_8,
  output PRINT
);


  assign EE_RAM_8 = I8;
  assign PRINT = I8;
endmodule

module Instrucao_A_ate_F (
  input  IA,
  input  IB,
  input  ID,
  input  I_F,
  input  c3,
  input  c4,
  output COMP,
  output M1_CTR8
);

  wire and_1_out, and_2_out, and_3_out, nor_1_out;

  nor nor_1 (nor_1_out, c3, c4);
  and and_1 (and_1_out, IB, c4);
  and and_2 (and_2_out, ID, c3);
  and and_3 (and_3_out, I_F, nor_1_out);
  or or_1 (COMP, IA, IB, ID, I_F);
  or or_2 (M1_CTR8, IA, and_1_out, and_2_out, and_3_out);
endmodule

module OP_Aritmetico_8bit (
  input  [7:0] A,
  input  [7:0] B,
  input  OP,
  output [7:0] R,
  output CS,
  output SS
);

  wire somador_8bit_1_c_out_7, somador_8bit_1_c_out_8;

  Somador_8bit somador_8bit_1 (
    .A(A), .B(B), .c_in_0(OP), .R(R), .c_out_7(somador_8bit_1_c_out_7), .c_out_8(somador_8bit_1_c_out_8));
  xor xor_1 (CS, somador_8bit_1_c_out_7, somador_8bit_1_c_out_8);
  xor xor_2 (SS, somador_8bit_1_c_out_8, OP);
endmodule

module Somador_8bit (
  input  [7:0] A,
  input  [7:0] B,
  input  c_in_0,
  output [7:0] R,
  output c_out_7,
  output c_out_8
);

  wire somador_1bit_1_c_out, somador_1bit_2_c_out, somador_1bit_3_c_out, somador_1bit_4_c_out,
       somador_1bit_5_c_out, somador_1bit_6_c_out, xor_1_out, xor_2_out, xor_3_out, xor_4_out, xor_5_out,
       xor_6_out, xor_7_out, xor_8_out;

  xor xor_1 (xor_1_out, B[0], c_in_0);
  xor xor_2 (xor_2_out, B[1], c_in_0);
  xor xor_3 (xor_3_out, B[2], c_in_0);
  xor xor_4 (xor_4_out, B[3], c_in_0);
  xor xor_5 (xor_5_out, B[4], c_in_0);
  xor xor_6 (xor_6_out, B[5], c_in_0);
  xor xor_7 (xor_7_out, B[6], c_in_0);
  xor xor_8 (xor_8_out, B[7], c_in_0);
  Somador_1bit somador_1bit_1 (.a(A[0]), .b(xor_1_out), .c_in(c_in_0), .s(R[0]), .c_out(somador_1bit_1_c_out));
  Somador_1bit somador_1bit_2 (
    .a(A[1]), .b(xor_2_out), .c_in(somador_1bit_1_c_out), .s(R[1]), .c_out(somador_1bit_2_c_out));
  Somador_1bit somador_1bit_3 (
    .a(A[2]), .b(xor_3_out), .c_in(somador_1bit_2_c_out), .s(R[2]), .c_out(somador_1bit_3_c_out));
  Somador_1bit somador_1bit_4 (
    .a(A[3]), .b(xor_4_out), .c_in(somador_1bit_3_c_out), .s(R[3]), .c_out(somador_1bit_4_c_out));
  Somador_1bit somador_1bit_5 (
    .a(A[4]), .b(xor_5_out), .c_in(somador_1bit_4_c_out), .s(R[4]), .c_out(somador_1bit_5_c_out));
  Somador_1bit somador_1bit_6 (
    .a(A[5]), .b(xor_6_out), .c_in(somador_1bit_5_c_out), .s(R[5]), .c_out(somador_1bit_6_c_out));
  Somador_1bit somador_1bit_7 (.a(A[6]), .b(xor_7_out), .c_in(somador_1bit_6_c_out), .s(R[6]), .c_out(c_out_7));
  Somador_1bit somador_1bit_8 (.a(A[7]), .b(xor_8_out), .c_in(c_out_7), .s(R[7]), .c_out(c_out_8));
endmodule

module Somador_1bit (
  input  a,
  input  b,
  input  c_in,
  output s,
  output c_out
);

  wire and_1_out, and_2_out, xor_1_out;

  xor xor_1 (xor_1_out, a, b);
  xor xor_2 (s, xor_1_out, c_in);
  and and_1 (and_1_out, c_in, xor_1_out);
  and and_2 (and_2_out, a, b);
  or or_1 (c_out, and_1_out, and_2_out);
endmodule

module Comp_8bit (
  input  [7:0] A,
  input  [7:0] B,
  output c0,
  output c1,
  output c2,
  output c3,
  output c4,
  output c5
);

  wire and_1_out, and_2_out, and_3_out, and_4_out, and_5_out, and_6_out, and_7_out, comp_1bit_1_a_maior,
       comp_1bit_1_iguais, comp_1bit_2_a_maior, comp_1bit_2_iguais, comp_1bit_3_a_maior, comp_1bit_3_iguais,
       comp_1bit_4_a_maior, comp_1bit_4_iguais, comp_1bit_5_a_maior, comp_1bit_5_iguais, comp_1bit_6_a_maior,
       comp_1bit_6_iguais, comp_1bit_7_a_maior, comp_1bit_7_iguais, comp_1bit_8_a_maior, comp_1bit_8_b_maior,
       comp_1bit_8_iguais, or_1_out, or_2_out, or_3_out, or_4_out, or_5_out, or_6_out;

  Comp_1bit comp_1bit_1 (
    .a(A[0]), .b(B[0]), .a_maior(comp_1bit_1_a_maior), .iguais(comp_1bit_1_iguais));  // open: b_maior
  Comp_1bit comp_1bit_2 (
    .a(A[1]), .b(B[1]), .a_maior(comp_1bit_2_a_maior), .iguais(comp_1bit_2_iguais));  // open: b_maior
  Comp_1bit comp_1bit_3 (
    .a(A[2]), .b(B[2]), .a_maior(comp_1bit_3_a_maior), .iguais(comp_1bit_3_iguais));  // open: b_maior
  Comp_1bit comp_1bit_4 (
    .a(A[3]), .b(B[3]), .a_maior(comp_1bit_4_a_maior), .iguais(comp_1bit_4_iguais));  // open: b_maior
  Comp_1bit comp_1bit_5 (
    .a(A[4]), .b(B[4]), .a_maior(comp_1bit_5_a_maior), .iguais(comp_1bit_5_iguais));  // open: b_maior
  Comp_1bit comp_1bit_6 (
    .a(A[5]), .b(B[5]), .a_maior(comp_1bit_6_a_maior), .iguais(comp_1bit_6_iguais));  // open: b_maior
  Comp_1bit comp_1bit_7 (
    .a(A[6]), .b(B[6]), .a_maior(comp_1bit_7_a_maior), .iguais(comp_1bit_7_iguais));  // open: b_maior
  Comp_1bit comp_1bit_8 (
    .a(A[7]), .b(B[7]), .a_maior(comp_1bit_8_a_maior), .iguais(comp_1bit_8_iguais),
    .b_maior(comp_1bit_8_b_maior));
  and and_1 (and_1_out, comp_1bit_1_a_maior, comp_1bit_2_iguais);
  or or_1 (or_1_out, and_1_out, comp_1bit_2_a_maior);
  and and_2 (and_2_out, or_1_out, comp_1bit_3_iguais);
  or or_2 (or_2_out, and_2_out, comp_1bit_3_a_maior);
  and and_3 (and_3_out, or_2_out, comp_1bit_4_iguais);
  or or_3 (or_3_out, and_3_out, comp_1bit_4_a_maior);
  and and_4 (and_4_out, or_3_out, comp_1bit_5_iguais);
  or or_4 (or_4_out, and_4_out, comp_1bit_5_a_maior);
  and and_5 (and_5_out, or_4_out, comp_1bit_6_iguais);
  or or_5 (or_5_out, and_5_out, comp_1bit_6_a_maior);
  and and_6 (and_6_out, or_5_out, comp_1bit_7_iguais);
  or or_6 (or_6_out, and_6_out, comp_1bit_7_a_maior);
  and and_7 (and_7_out, or_6_out, comp_1bit_8_iguais);
  or or_7 (c0, and_7_out, comp_1bit_8_a_maior);
  or or_8 (c4, comp_1bit_8_b_maior, and_7_out);
  and and_8 (c2, comp_1bit_1_iguais, comp_1bit_2_iguais, comp_1bit_3_iguais, comp_1bit_4_iguais, comp_1bit_5_iguais, comp_1bit_6_iguais, comp_1bit_7_iguais, comp_1bit_8_iguais);
  nor nor_1 (c3, A[0], A[1], A[2], A[3], A[4], A[5], A[6], A[7]);
  nor nor_2 (c1, c0, c2);
  nor nor_3 (c5, c4, c2);
endmodule

module Comp_1bit (
  input  a,
  input  b,
  output a_maior,
  output iguais,
  output b_maior
);

  wire xor_1_out;

  xor xor_1 (xor_1_out, a, b);
  not not_1 (iguais, xor_1_out);
  and and_1 (a_maior, a, xor_1_out);
  and and_2 (b_maior, xor_1_out, b);
endmodule
